// Logisim project Labo2.circ as structural Verilog: 11 circuits, main circuit ADD8BITS
module main (
);


  // Notes on the sheet:
  //   Attention, votre version de Logisim
  //   ne contient pas de tracker. Si vous
  //   enregistrez votre projet, toutes les
  //   informations du tracker seront
  //   définitivement effacées.
endmodule

module prout (
);


  // Notes on the sheet:
  //   Attention, votre version de Logisim
  //   ne contient pas de tracker. Si vous
  //   enregistrez votre projet, toutes les
  //   informations du tracker seront
  //   définitivement effacées.
endmodule

module ADD4BITS (
  input  [3:0] A,
  input  [3:0] B,
  input  C_in,
  output [3:0] D,
  output C_out
);

  wire add1bit_1_c_out, add1bit_2_c_out, add1bit_3_c_out;

  ADD1BIT add1bit_1 (.A(A[0]), .B(B[0]), .C_in(C_in), .D(D[0]), .C_out(add1bit_1_c_out));
  ADD1BIT add1bit_2 (.A(A[1]), .B(B[1]), .C_in(add1bit_1_c_out), .D(D[1]), .C_out(add1bit_2_c_out));
  ADD1BIT add1bit_3 (.A(A[2]), .B(B[2]), .C_in(add1bit_2_c_out), .D(D[2]), .C_out(add1bit_3_c_out));
  ADD1BIT add1bit_4 (.A(A[3]), .B(B[3]), .C_in(add1bit_3_c_out), .D(D[3]), .C_out(C_out));

  // Notes on the sheet:
  //   Attention, votre version de Logisim
  //   ne contient pas de tracker. Si vous
  //   enregistrez votre projet, toutes les
  //   informations du tracker seront
  //   définitivement effacées.
endmodule

module ADD1BIT (
  input  A,
  input  B,
  input  C_in,
  output D,
  output C_out
);

  wire and_1_out, and_2_out, and_3_out, xor_1_out;

  xor xor_1 (xor_1_out, A, B);
  and and_1 (and_1_out, A, B);
  and and_2 (and_2_out, A, C_in);
  and and_3 (and_3_out, B, C_in);
  or or_1 (C_out, and_1_out, and_2_out, and_3_out);
  xor xor_2 (D, xor_1_out, C_in);

  // Notes on the sheet:
  //   Attention, votre version de Logisim
  //   ne contient pas de tracker. Si vous
  //   enregistrez votre projet, toutes les
  //   informations du tracker seront
  //   définitivement effacées.
endmodule

module ADD16BITS (
  input  [15:0] A,
  input  [15:0] B,
  input  C_in,
  output [15:0] D,
  output C_out
);

  wire add4bits_1_c_out, add4bits_2_c_out, add4bits_3_c_out;

  ADD4BITS add4bits_1 (.A(A[3:0]), .B(B[3:0]), .C_in(C_in), .D(D[3:0]), .C_out(add4bits_1_c_out));
  ADD4BITS add4bits_2 (.A(A[7:4]), .B(B[7:4]), .C_in(add4bits_1_c_out), .D(D[7:4]), .C_out(add4bits_2_c_out));
  ADD4BITS add4bits_3 (.A(A[11:8]), .B(B[11:8]), .C_in(add4bits_2_c_out), .D(D[11:8]), .C_out(add4bits_3_c_out));
  ADD4BITS add4bits_4 (.A(A[15:12]), .B(B[15:12]), .C_in(add4bits_3_c_out), .D(D[15:12]), .C_out(C_out));

  // Notes on the sheet:
  //   Attention, votre version de Logisim
  //   ne contient pas de tracker. Si vous
  //   enregistrez votre projet, toutes les
  //   informations du tracker seront
  //   définitivement effacées.
endmodule

module ADD8BITS (
  input  [7:0] A,
  input  [7:0] B,
  input  C_in,
  output [7:0] D,
  output C_out
);

  wire add4bits_1_c_out, add4bits_2_c_out;

  ADD4BITS add4bits_1 (.A(A[3:0]), .B(B[3:0]), .C_in(C_in), .D(D[3:0]), .C_out(add4bits_1_c_out));
  ADD4BITS add4bits_2 (.A(A[7:4]), .B(B[7:4]), .C_in(add4bits_1_c_out), .D(D[7:4]), .C_out(add4bits_2_c_out));

  // Notes on the sheet:
  //   Attention, votre version de Logisim
  //   ne contient pas de tracker. Si vous
  //   enregistrez votre projet, toutes les
  //   informations du tracker seront
  //   définitivement effacées.
endmodule

module ADD_SUB8BITS (
  input  S,
  input  [7:0] A,
  input  [7:0] B,
  input  in_4,
  input  in_5,
  output [7:0] out_6
);

  wire add4bits_1_c_out, add4bits_2_c_out, comp2_4bits_1_p1;
  wire [7:0] comp2_4bits_1_p2;

  // COMP2_4BITS comp2_4bits_1: pin names not known; wires that end beside it: comp2_4bits_1_p1, comp2_4bits_1_p2
  ADD4BITS add4bits_1 (.A(A[3:0]), .B(comp2_4bits_1_p2[3:0]), .C_in(in_5), .D(out_6[3:0]), .C_out(add4bits_1_c_out));
  ADD4BITS add4bits_2 (
    .A(A[7:4]), .B(comp2_4bits_1_p2[7:4]), .C_in(add4bits_1_c_out), .D(out_6[7:4]), .C_out(add4bits_2_c_out));
  CMP2_4BITS cmp2_4bits_1 ();  // open: S, A, B, out_4, C_out, out_6

  // Notes on the sheet:
  //   Attention, votre version de Logisim
  //   ne contient pas de tracker. Si vous
  //   enregistrez votre projet, toutes les
  //   informations du tracker seront
  //   définitivement effacées.
endmodule

module CMP2_4BITS (
  input  S,
  input  [3:0] A,
  input  [3:0] B,
  output [3:0] out_4,
  output C_out,
  output [7:0] out_6
);

  wire add1bit_1_c_out, add1bit_2_c_out, add1bit_3_c_out, add8bits_1_c_out, xor_1_out, xor_2_out, xor_3_out,
       xor_4_out;
  wire [7:0] not_1_out, undriven;

  xor xor_1 (xor_1_out, S, A[0]);
  xor xor_2 (xor_2_out, S, A[1]);
  xor xor_3 (xor_3_out, S, A[2]);
  xor xor_4 (xor_4_out, S, A[3]);
  assign not_1_out = ~undriven;  // NOT_Gate not_1, 8 bits wide
  ADD1BIT add1bit_1 (.A(xor_1_out), .B(B[0]), .C_in(S), .D(out_4[0]), .C_out(add1bit_1_c_out));
  ADD1BIT add1bit_2 (.A(xor_2_out), .B(B[1]), .C_in(add1bit_1_c_out), .D(out_4[1]), .C_out(add1bit_2_c_out));
  ADD1BIT add1bit_3 (.A(xor_3_out), .B(B[2]), .C_in(add1bit_2_c_out), .D(out_4[2]), .C_out(add1bit_3_c_out));
  ADD1BIT add1bit_4 (.A(xor_4_out), .B(B[3]), .C_in(add1bit_3_c_out), .D(out_4[3]), .C_out(C_out));
  ADD8BITS add8bits_1 (.A(not_1_out), .B(8'h1), .C_in(1'b0), .D(out_6), .C_out(add8bits_1_c_out));

  // Notes on the sheet:
  //   Attention, votre version de Logisim
  //   ne contient pas de tracker. Si vous
  //   enregistrez votre projet, toutes les
  //   informations du tracker seront
  //   définitivement effacées.
endmodule

module ADD_SUB4BITS (
  input  in_1,
  input  [3:0] in_2,
  input  [3:0] in_3,
  output [3:0] D
);

  wire [3:0] xor_1_out;

  xor xor_1 (xor_1_out[0], in_1, in_2[0]);
  xor xor_2 (xor_1_out[1], in_1, in_2[1]);
  xor xor_3 (xor_1_out[2], in_1, in_2[2]);
  xor xor_4 (xor_1_out[3], in_1, in_2[3]);
  ADD4BITS add4bits_1 (.A(xor_1_out), .B(in_3), .C_in(in_1), .D(D));  // open: C_out

  // Notes on the sheet:
  //   Attention, votre version de Logisim
  //   ne contient pas de tracker. Si vous
  //   enregistrez votre projet, toutes les
  //   informations du tracker seront
  //   définitivement effacées.
endmodule

module COMP2_4BITS (
  input  S,
  input  [3:0] A,
  output [3:0] D,
  output C_out
);

  xor xor_1 (D[0], S, A[0]);
  xor xor_2 (D[1], S, A[1]);
  xor xor_3 (D[2], S, A[2]);
  xor xor_4 (D[3], S, A[3]);

  assign C_out = S;

  // Notes on the sheet:
  //   Attention, votre version de Logisim
  //   ne contient pas de tracker. Si vous
  //   enregistrez votre projet, toutes les
  //   informations du tracker seront
  //   définitivement effacées.
endmodule

module COMP2_8BITS (
  input  S,
  input  [7:0] A,
  output [7:0] D,
  output C_out
);

  wire comp2_4bits_1_c_out;

  COMP2_4BITS comp2_4bits_1 (.S(S), .A(A[3:0]), .D(D[3:0]), .C_out(comp2_4bits_1_c_out));
  COMP2_4BITS comp2_4bits_2 (.S(comp2_4bits_1_c_out), .A(A[7:4]), .D(D[7:4]), .C_out(C_out));

  // Notes on the sheet:
  //   Attention, votre version de Logisim
  //   ne contient pas de tracker. Si vous
  //   enregistrez votre projet, toutes les
  //   informations du tracker seront
  //   définitivement effacées.
endmodule
