// Logisim project Labo2_Rouvinez_Meyer.circ as structural Verilog: 15 circuits, main circuit CHRONO_ADDSUB_8BITS
module main (
);


  // Notes on the sheet:
  //   Attention, votre version de Logisim
  //   ne contient pas de tracker. Si vous
  //   enregistrez votre projet, toutes les
  //   informations du tracker seront
  //   définitivement effacées.
endmodule

module ADD4BITS (
  input  [3:0] A,
  input  [3:0] B,
  input  C_in,
  output [3:0] D,
  output C_out
);

  wire add1bit_1_c_out, add1bit_2_c_out, add1bit_3_c_out;

  ADD1BIT add1bit_1 (.A(A[0]), .B(B[0]), .C_in(C_in), .D(D[0]), .C_out(add1bit_1_c_out));
  ADD1BIT add1bit_2 (.A(A[1]), .B(B[1]), .C_in(add1bit_1_c_out), .D(D[1]), .C_out(add1bit_2_c_out));
  ADD1BIT add1bit_3 (.A(A[2]), .B(B[2]), .C_in(add1bit_2_c_out), .D(D[2]), .C_out(add1bit_3_c_out));
  ADD1BIT add1bit_4 (.A(A[3]), .B(B[3]), .C_in(add1bit_3_c_out), .D(D[3]), .C_out(C_out));

  // Notes on the sheet:
  //   Attention, votre version de Logisim
  //   ne contient pas de tracker. Si vous
  //   enregistrez votre projet, toutes les
  //   informations du tracker seront
  //   définitivement effacées.
endmodule

module ADD1BIT (
  input  A,
  input  B,
  input  C_in,
  output D,
  output C_out
);

  wire and_1_out, and_2_out, and_3_out, xor_1_out;

  xor xor_1 (xor_1_out, A, B);
  and and_1 (and_1_out, A, B);
  and and_2 (and_2_out, A, C_in);
  and and_3 (and_3_out, B, C_in);
  or or_1 (C_out, and_1_out, and_2_out, and_3_out);
  xor xor_2 (D, xor_1_out, C_in);

  // Notes on the sheet:
  //   Attention, votre version de Logisim
  //   ne contient pas de tracker. Si vous
  //   enregistrez votre projet, toutes les
  //   informations du tracker seront
  //   définitivement effacées.
endmodule

module ADD16BITS (
  input  [15:0] A,
  input  [15:0] B,
  input  C_in,
  output [15:0] D,
  output C_out
);

  wire add4bits_1_c_out, add4bits_2_c_out, add4bits_3_c_out;

  ADD4BITS add4bits_1 (.A(A[3:0]), .B(B[3:0]), .C_in(C_in), .D(D[3:0]), .C_out(add4bits_1_c_out));
  ADD4BITS add4bits_2 (.A(A[7:4]), .B(B[7:4]), .C_in(add4bits_1_c_out), .D(D[7:4]), .C_out(add4bits_2_c_out));
  ADD4BITS add4bits_3 (.A(A[11:8]), .B(B[11:8]), .C_in(add4bits_2_c_out), .D(D[11:8]), .C_out(add4bits_3_c_out));
  ADD4BITS add4bits_4 (.A(A[15:12]), .B(B[15:12]), .C_in(add4bits_3_c_out), .D(D[15:12]), .C_out(C_out));

  // Notes on the sheet:
  //   Attention, votre version de Logisim
  //   ne contient pas de tracker. Si vous
  //   enregistrez votre projet, toutes les
  //   informations du tracker seront
  //   définitivement effacées.
endmodule

module ADD8BITS (
  input  [7:0] A,
  input  [7:0] B,
  input  C_in,
  output [7:0] D,
  output C_out
);

  wire add4bits_1_c_out;

  ADD4BITS add4bits_1 (.A(A[3:0]), .B(B[3:0]), .C_in(C_in), .D(D[3:0]), .C_out(add4bits_1_c_out));
  ADD4BITS add4bits_2 (.A(A[7:4]), .B(B[7:4]), .C_in(add4bits_1_c_out), .D(D[7:4]), .C_out(C_out));

  // Notes on the sheet:
  //   Attention, votre version de Logisim
  //   ne contient pas de tracker. Si vous
  //   enregistrez votre projet, toutes les
  //   informations du tracker seront
  //   définitivement effacées.
endmodule

module ADD_SUB8BITS (
  input  S,
  input  [7:0] A,
  input  [7:0] B,
  output [7:0] out_4,
  output C_out
);

  wire add4bits_1_c_out, comp2_8bits_1_c_out;
  wire [7:0] comp2_8bits_1_d;

  COMP2_8BITS comp2_8bits_1 (.S(S), .A(B), .D(comp2_8bits_1_d), .C_out(comp2_8bits_1_c_out));
  ADD4BITS add4bits_1 (
    .A(A[3:0]), .B(comp2_8bits_1_d[3:0]), .C_in(comp2_8bits_1_c_out), .D(out_4[3:0]), .C_out(add4bits_1_c_out));
  ADD4BITS add4bits_2 (.A(A[7:4]), .B(comp2_8bits_1_d[7:4]), .C_in(add4bits_1_c_out), .D(out_4[7:4]), .C_out(C_out));

  // Notes on the sheet:
  //   Attention, votre version de Logisim
  //   ne contient pas de tracker. Si vous
  //   enregistrez votre projet, toutes les
  //   informations du tracker seront
  //   définitivement effacées.
endmodule

module OLD_CMP2_4BITS (
  input  S,
  input  [3:0] A,
  input  [3:0] B,
  output [3:0] out_4,
  output C_out
);

  wire add1bit_1_c_out, add1bit_2_c_out, add1bit_3_c_out, xor_1_out, xor_2_out, xor_3_out, xor_4_out;

  xor xor_1 (xor_1_out, S, A[0]);
  xor xor_2 (xor_2_out, S, A[1]);
  xor xor_3 (xor_3_out, S, A[2]);
  xor xor_4 (xor_4_out, S, A[3]);
  ADD1BIT add1bit_1 (.A(xor_1_out), .B(B[0]), .C_in(S), .D(out_4[0]), .C_out(add1bit_1_c_out));
  ADD1BIT add1bit_2 (.A(xor_2_out), .B(B[1]), .C_in(add1bit_1_c_out), .D(out_4[1]), .C_out(add1bit_2_c_out));
  ADD1BIT add1bit_3 (.A(xor_3_out), .B(B[2]), .C_in(add1bit_2_c_out), .D(out_4[2]), .C_out(add1bit_3_c_out));
  ADD1BIT add1bit_4 (.A(xor_4_out), .B(B[3]), .C_in(add1bit_3_c_out), .D(out_4[3]), .C_out(C_out));

  // Notes on the sheet:
  //   Attention, votre version de Logisim
  //   ne contient pas de tracker. Si vous
  //   enregistrez votre projet, toutes les
  //   informations du tracker seront
  //   définitivement effacées.
endmodule

module ADD_SUB4BITS (
  input  in_1,
  input  [3:0] in_2,
  input  [3:0] in_3,
  output [3:0] D
);

  wire [3:0] xor_1_out;

  xor xor_1 (xor_1_out[0], in_1, in_2[0]);
  xor xor_2 (xor_1_out[1], in_1, in_2[1]);
  xor xor_3 (xor_1_out[2], in_1, in_2[2]);
  xor xor_4 (xor_1_out[3], in_1, in_2[3]);
  ADD4BITS add4bits_1 (.A(xor_1_out), .B(in_3), .C_in(in_1), .D(D));  // open: C_out

  // Notes on the sheet:
  //   Attention, votre version de Logisim
  //   ne contient pas de tracker. Si vous
  //   enregistrez votre projet, toutes les
  //   informations du tracker seront
  //   définitivement effacées.
endmodule

module COMP2_4BITS (
  input  S,
  input  [3:0] A,
  output [3:0] D,
  output C_out
);

  xor xor_1 (D[0], S, A[0]);
  xor xor_2 (D[1], S, A[1]);
  xor xor_3 (D[2], S, A[2]);
  xor xor_4 (D[3], S, A[3]);

  assign C_out = S;

  // Notes on the sheet:
  //   Attention, votre version de Logisim
  //   ne contient pas de tracker. Si vous
  //   enregistrez votre projet, toutes les
  //   informations du tracker seront
  //   définitivement effacées.
endmodule

module COMP2_8BITS (
  input  S,
  input  [7:0] A,
  output [7:0] D,
  output C_out
);

  wire comp2_4bits_1_c_out;

  COMP2_4BITS comp2_4bits_1 (.S(S), .A(A[3:0]), .D(D[3:0]), .C_out(comp2_4bits_1_c_out));
  COMP2_4BITS comp2_4bits_2 (.S(comp2_4bits_1_c_out), .A(A[7:4]), .D(D[7:4]), .C_out(C_out));

  // Notes on the sheet:
  //   Attention, votre version de Logisim
  //   ne contient pas de tracker. Si vous
  //   enregistrez votre projet, toutes les
  //   informations du tracker seront
  //   définitivement effacées.
endmodule

module CHKSM_3x8BITS (
  input  [7:0] A,
  input  [7:0] B,
  input  [7:0] C,
  output out_4,
  output [7:0] D
);

  wire ADD8BITS1_c_out, ADD8BITS2_c_out;
  wire [7:0] ADD8BITS1_d, ADD8BITS2_d;

  ADD8BITS ADD8BITS1 (.A(A), .B(B), .D(ADD8BITS1_d), .C_out(ADD8BITS1_c_out));  // open: C_in
  ADD8BITS ADD8BITS2 (.A(ADD8BITS1_d), .B(C), .D(ADD8BITS2_d), .C_out(ADD8BITS2_c_out));  // open: C_in
  or or_1 (out_4, ADD8BITS1_c_out, ADD8BITS2_c_out);
  ADD_SUB8BITS add_sub8bits_1 (.S(1'b1), .A({8{1'b0}}), .B(ADD8BITS2_d), .out_4(D));  // open: C_out

  // Notes on the sheet:
  //   Attention, votre version de Logisim
  //   ne contient pas de tracker. Si vous
  //   enregistrez votre projet, toutes les
  //   informations du tracker seront
  //   définitivement effacées.
endmodule

module VERIF_INTEG_4x8BITS (
  input  [7:0] A,
  input  [7:0] B,
  input  [7:0] C,
  input  [7:0] D,
  output out_5
);

  wire [7:0] add8bits_1_d, add8bits_2_d, add8bits_3_d;

  ADD8BITS add8bits_1 (.A(A), .B(B), .D(add8bits_1_d));  // open: C_in, C_out
  ADD8BITS add8bits_2 (.A(add8bits_1_d), .B(C), .D(add8bits_2_d));  // open: C_in, C_out
  ADD8BITS add8bits_3 (.A(add8bits_2_d), .B(D), .D(add8bits_3_d));  // open: C_in, C_out
  IS_ZERO_8BITS is_zero_8bits_1 (.A(add8bits_3_d), .D(out_5));

  // Notes on the sheet:
  //   Attention, votre version de Logisim
  //   ne contient pas de tracker. Si vous
  //   enregistrez votre projet, toutes les
  //   informations du tracker seront
  //   définitivement effacées.
endmodule

module IS_ZERO_8BITS (
  input  [7:0] A,
  output D
);

  wire or_1_out, or_2_out, or_3_out, or_4_out, or_5_out, or_6_out, or_7_out;

  or or_1 (or_1_out, A[0], A[1]);
  or or_2 (or_2_out, A[2], A[3]);
  or or_3 (or_3_out, A[4], A[5]);
  or or_4 (or_4_out, A[6], A[7]);
  or or_5 (or_5_out, or_1_out, or_2_out);
  or or_6 (or_6_out, or_3_out, or_4_out);
  or or_7 (or_7_out, or_5_out, or_6_out);
  not not_1 (D, or_7_out);

  // Notes on the sheet:
  //   Attention, votre version de Logisim
  //   ne contient pas de tracker. Si vous
  //   enregistrez votre projet, toutes les
  //   informations du tracker seront
  //   définitivement effacées.
endmodule

module CHRONO_ADDSUB_8BITS (
  output [7:0] D,
  output C_out
);

  wire clk_out;
  wire [7:0] counter_1_q;

  Clock #(.highDuration(4), .lowDuration(4)) clk (.out(clk_out));
  Clock sysclk ();  // open: out
  Counter counter_1 (
    .clr(1'b0), .load(1'b0), .up(1'b1), .count(1'b1), .clk(clk_out), .Q(counter_1_q));  // open: D, carry
  ADD_SUB8BITS add_sub8bits_1 (.S(1'b0), .A(counter_1_q), .B(8'h1), .out_4(D), .C_out(C_out));

  // Notes on the sheet:
  //   Attention, votre version de Logisim
  //   ne contient pas de tracker. Si vous
  //   enregistrez votre projet, toutes les
  //   informations du tracker seront
  //   définitivement effacées.
endmodule

module CHRONO_CHKSM_3x8BITS (
  output [7:0] D
);

  wire clk_out;
  wire [7:0] counter_1_q;

  Clock #(.highDuration(4), .lowDuration(4)) clk (.out(clk_out));
  Clock sysclk ();  // open: out
  Counter counter_1 (
    .clr(1'b0), .load(1'b0), .up(1'b1), .count(1'b1), .clk(clk_out), .Q(counter_1_q));  // open: D, carry
  CHKSM_3x8BITS chksm_3x8bits_1 (.A(counter_1_q), .B(counter_1_q), .C(counter_1_q), .out_4(D[0]));  // open: D
  // Pins of 1 and 8 bits meet at D

  // Notes on the sheet:
  //   Attention, votre version de Logisim
  //   ne contient pas de tracker. Si vous
  //   enregistrez votre projet, toutes les
  //   informations du tracker seront
  //   définitivement effacées.
endmodule
