// Logisim project labo3.circ as structural Verilog: 13 circuits, main circuit main
module main (
  input  [5:0] OPCODE,
  input  [3:0] A,
  input  [3:0] B,
  output ERROR,
  output [3:0] C
);

  wire ADDSUBALU_c_out, ADDSUBALU_r3, ADDSUBALU_zero, bitselector_1_out, bitselector_2_out;
  wire [3:0] ADDSUBALU_r, comparateur_1_cmp, custom_1_s, logic_4bits_1_p4;

  BitSelector #(.width(4)) bitselector_1 (.in(B), .out(bitselector_1_out), .sel(2'b11));
  BitSelector #(.width(4)) bitselector_2 (.in(A), .out(bitselector_2_out), .sel(2'b11));
  COMPARATEUR comparateur_1 (
    .Carry(ADDSUBALU_c_out), .R3(ADDSUBALU_r3), .ZERO(ADDSUBALU_zero), .Opcode_2_0(OPCODE[2:0]),
    .A(bitselector_2_out), .B(bitselector_1_out), .Cmp(comparateur_1_cmp));
  // LOGIC_4BITS logic_4bits_1: pin names not known; wires that end beside it: OPCODE[1:0], A, B, logic_4bits_1_p4
  CUSTOM custom_1 (.A(A), .B(B), .S(custom_1_s));
  ADDSUB_ALU ADDSUBALU (
    .OPCODE_3_2(OPCODE[3:2]), .A(A), .B(B), .OVERFLOW(ERROR), .R(ADDSUBALU_r), .C_out(ADDSUBALU_c_out),
    .R3(ADDSUBALU_r3), .ZERO(ADDSUBALU_zero));
  Multiplexer #(.select(2), .width(4), .enable("false")) multiplexer_1 (
    .in0(ADDSUBALU_r), .in1(comparateur_1_cmp), .in2(logic_4bits_1_p4), .in3(custom_1_s), .out(C),
    .sel(OPCODE[5:4]));

  // Notes on the sheet:
  //   Attention, votre version de Logisim
  //   ne contient pas de tracker. Si vous
  //   enregistrez votre projet, toutes les
  //   informations du tracker seront
  //   définitivement effacées.
endmodule

module CUSTOM (
  input  [3:0] A,
  input  [3:0] B,
  output [3:0] S
);

  wire add1bit_1_c_out, add1bit_1_d, add1bit_2_c_out, add1bit_2_d, add1bit_3_c_out, add1bit_3_d,
       add1bit_4_c_out, add1bit_5_c_out, out03A_c_out, out03A_d, out03B_c_out, out03B_d;

  ADD1BIT out03A (.A(A[0]), .B(A[1]), .C_in(A[2]), .D(out03A_d), .C_out(out03A_c_out));
  ADD1BIT out03B (.A(A[3]), .B(B[0]), .C_in(B[1]), .D(out03B_d), .C_out(out03B_c_out));
  ADD1BIT add1bit_1 (.A(B[2]), .B(B[3]), .D(add1bit_1_d), .C_out(add1bit_1_c_out));  // open: C_in
  ADD1BIT add1bit_2 (.A(out03A_d), .B(out03B_d), .D(add1bit_2_d), .C_out(add1bit_2_c_out));  // open: C_in
  ADD1BIT add1bit_3 (
    .A(out03A_c_out), .B(out03B_c_out), .C_in(add1bit_2_c_out), .D(add1bit_3_d), .C_out(add1bit_3_c_out));
  ADD1BIT add1bit_4 (.A(add1bit_2_d), .B(add1bit_1_d), .D(S[0]), .C_out(add1bit_4_c_out));  // open: C_in
  ADD1BIT add1bit_5 (.A(add1bit_3_d), .B(add1bit_1_c_out), .C_in(add1bit_4_c_out), .D(S[1]), .C_out(add1bit_5_c_out));
  ADD1BIT add1bit_6 (.A(add1bit_3_c_out), .C_in(add1bit_5_c_out), .D(S[2]), .C_out(S[3]));  // open: B

  // Notes on the sheet:
  //   Attention, votre version de Logisim
  //   ne contient pas de tracker. Si vous
  //   enregistrez votre projet, toutes les
  //   informations du tracker seront
  //   définitivement effacées.
endmodule

module ADD1BIT (
  input  A,
  input  B,
  input  C_in,
  output D,
  output C_out
);

  wire and_1_out, and_2_out, and_3_out, xor_1_out;

  xor xor_1 (xor_1_out, A, B);
  and and_1 (and_1_out, A, B);
  and and_2 (and_2_out, A, C_in);
  and and_3 (and_3_out, B, C_in);
  or or_1 (C_out, and_1_out, and_2_out, and_3_out);
  xor xor_2 (D, xor_1_out, C_in);

  // Notes on the sheet:
  //   Attention, votre version de Logisim
  //   ne contient pas de tracker. Si vous
  //   enregistrez votre projet, toutes les
  //   informations du tracker seront
  //   définitivement effacées.
endmodule

module ADDSUB_ALU (
  input  [1:0] OPCODE_3_2,
  input  [3:0] A,
  input  [3:0] B,
  output OVERFLOW,
  output [3:0] R,
  output C_out,
  output R3,
  output ZERO
);

  wire bitselector_1_out, bitselector_2_out, bitselector_3_out, bitselector_4_out, overfaddsub_4bits_1_d;

  BitSelector #(.width(2)) bitselector_1 (.in(OPCODE_3_2), .out(bitselector_1_out), .sel(1'b1));
  BitSelector #(.width(4)) bitselector_2 (.in(A), .out(bitselector_2_out), .sel(2'b11));
  BitSelector #(.width(4)) bitselector_3 (.in(B), .out(bitselector_3_out), .sel(2'b11));
  ADD_SUB4BITS add_sub4bits_1 (.Sub(bitselector_1_out), .A(A), .B(B), .D(R), .C_out(C_out));
  BitSelector #(.width(2)) bitselector_4 (.in(OPCODE_3_2), .out(bitselector_4_out), .sel(1'b0));
  OVERFADDSUB_4BITS overfaddsub_4bits_1 (
    .Sub(bitselector_1_out), .A(bitselector_2_out), .B(bitselector_3_out), .R3(R3), .D(overfaddsub_4bits_1_d));
  Multiplexer #(.enable("false")) multiplexer_1 (
    .in0(overfaddsub_4bits_1_d), .in1(C_out), .out(OVERFLOW), .sel(bitselector_4_out));
  BitSelector #(.width(4)) bitselector_5 (.in(R), .out(R3), .sel(2'b11));
  ISZERO_4BITS iszero_4bits_1 (.A(R), .D(ZERO));

  // Notes on the sheet:
  //   Attention, votre version de Logisim
  //   ne contient pas de tracker. Si vous
  //   enregistrez votre projet, toutes les
  //   informations du tracker seront
  //   définitivement effacées.
endmodule

module ADD_SUB4BITS (
  input  Sub,
  input  [3:0] A,
  input  [3:0] B,
  output [3:0] D,
  output C_out
);

  wire [3:0] comp2_4bits_1_d;

  COMP2_4BITS comp2_4bits_1 (.S(Sub), .A(B), .D(comp2_4bits_1_d));
  ADD4BITS add4bits_1 (.A(A), .B(comp2_4bits_1_d), .D(D), .C_out(C_out));  // open: C_in

  // Notes on the sheet:
  //   Attention, votre version de Logisim
  //   ne contient pas de tracker. Si vous
  //   enregistrez votre projet, toutes les
  //   informations du tracker seront
  //   définitivement effacées.
endmodule

module ADD4BITS (
  input  [3:0] A,
  input  [3:0] B,
  input  C_in,
  output [3:0] D,
  output C_out
);

  wire add1bit_1_c_out, add1bit_2_c_out, add1bit_3_c_out;

  ADD1BIT add1bit_1 (.A(A[0]), .B(B[0]), .C_in(C_in), .D(D[0]), .C_out(add1bit_1_c_out));
  ADD1BIT add1bit_2 (.A(A[1]), .B(B[1]), .C_in(add1bit_1_c_out), .D(D[1]), .C_out(add1bit_2_c_out));
  ADD1BIT add1bit_3 (.A(A[2]), .B(B[2]), .C_in(add1bit_2_c_out), .D(D[2]), .C_out(add1bit_3_c_out));
  ADD1BIT add1bit_4 (.A(A[3]), .B(B[3]), .C_in(add1bit_3_c_out), .D(D[3]), .C_out(C_out));

  // Notes on the sheet:
  //   Attention, votre version de Logisim
  //   ne contient pas de tracker. Si vous
  //   enregistrez votre projet, toutes les
  //   informations du tracker seront
  //   définitivement effacées.
endmodule

module COMP2_4BITS (
  input  S,
  input  [3:0] A,
  output [3:0] D
);

  wire [3:0] xor_1_out;

  xor xor_1 (xor_1_out[0], S, A[0]);
  xor xor_2 (xor_1_out[1], S, A[1]);
  xor xor_3 (xor_1_out[2], S, A[2]);
  xor xor_4 (xor_1_out[3], S, A[3]);
  ADD4BITS add4bits_1 (.A(xor_1_out), .C_in(S), .D(D));  // open: B, C_out

  // Notes on the sheet:
  //   Attention, votre version de Logisim
  //   ne contient pas de tracker. Si vous
  //   enregistrez votre projet, toutes les
  //   informations du tracker seront
  //   définitivement effacées.
endmodule

module ISZERO_4BITS (
  input  [3:0] A,
  output D
);

  wire or_1_out, or_2_out;

  or or_1 (or_1_out, A[0], A[1]);
  or or_2 (or_2_out, A[2], A[3]);
  nor nor_1 (D, or_1_out, or_2_out);

  // Notes on the sheet:
  //   Attention, votre version de Logisim
  //   ne contient pas de tracker. Si vous
  //   enregistrez votre projet, toutes les
  //   informations du tracker seront
  //   définitivement effacées.
endmodule

module OVERFADDSUB_4BITS (
  input  Sub,
  input  A,
  input  B,
  input  R3,
  output D
);

  wire and_1_out, and_2_out, not_1_out, not_2_out, not_3_out, xor_1_out, xor_2_out;

  not not_1 (not_1_out, B);
  not not_2 (not_2_out, A);
  not not_3 (not_3_out, R3);
  xor xor_1 (xor_1_out, Sub, not_1_out);
  xor xor_2 (xor_2_out, B, Sub);
  and and_1 (and_1_out, not_2_out, xor_1_out, R3);
  and and_2 (and_2_out, A, xor_2_out, not_3_out);
  or or_1 (D, and_1_out, and_2_out);

  // Notes on the sheet:
  //   Attention, votre version de Logisim
  //   ne contient pas de tracker. Si vous
  //   enregistrez votre projet, toutes les
  //   informations du tracker seront
  //   définitivement effacées.
endmodule

module COMPARATEUR (
  input  Carry,
  input  R3,
  input  ZERO,
  input  [2:0] Opcode_2_0,
  input  A,
  input  B,
  output [3:0] Cmp
);

  wire and_1_out, and_2_out, bitselector_1_out, multiplexer_1_out, not_1_out, not_2_out, not_3_out, or_1_out,
       xnor_1_out, xor_1_out, xor_2_out, xor_3_out;

  BitSelector #(.width(3)) bitselector_1 (.in(Opcode_2_0), .out(bitselector_1_out), .sel(2'b00));
  not not_1 (not_1_out, bitselector_1_out);
  xor xor_1 (xor_1_out, bitselector_1_out, A);
  xor xor_2 (xor_2_out, not_1_out, B);
  xor xor_3 (xor_3_out, bitselector_1_out, R3);
  and and_1 (and_1_out, xor_1_out, xor_2_out);
  xnor xnor_1 (xnor_1_out, A, B);
  and and_2 (and_2_out, xor_3_out, xnor_1_out);
  or or_1 (or_1_out, and_1_out, and_2_out);
  not not_2 (not_2_out, ZERO);
  not not_3 (not_3_out, Carry);
  Multiplexer #(.select(3), .enable("false")) multiplexer_1 (
    .in1(or_1_out), .in2(or_1_out), .in3(not_2_out), .in4(ZERO), .in5(Carry), .in6(not_3_out),
    .out(multiplexer_1_out), .sel(Opcode_2_0));  // open: in0, in7
  ADD4BITS add4bits_1 (.A(4'b0000), .C_in(multiplexer_1_out), .D(Cmp));  // open: B, C_out

  // Notes on the sheet:
  //   Attention, votre version de Logisim
  //   ne contient pas de tracker. Si vous
  //   enregistrez votre projet, toutes les
  //   informations du tracker seront
  //   définitivement effacées.
endmodule

module CUSTOM_OPT (
  input  [3:0] A,
  input  [3:0] B,
  output [3:0] D
);

  wire add1bit_1_c_out, add1bit_1_d, add1bit_2_c_out, add1bit_2_d, add1bit_3_c_out, add1bit_3_d,
       add1bit_4_c_out, add1bit_4_d, add1bit_5_p1, add1bit_5_p4, add1bit_5_p5, add1bit_6_c_out,
       add1bit_7_c_out;

  ADD1BIT add1bit_1 (.A(A[0]), .B(A[1]), .C_in(A[2]), .D(add1bit_1_d), .C_out(add1bit_1_c_out));
  ADD1BIT add1bit_2 (.A(A[3]), .B(B[0]), .C_in(B[1]), .D(add1bit_2_d), .C_out(add1bit_2_c_out));
  ADD1BIT add1bit_3 (.A(B[2]), .B(B[3]), .C_in(add1bit_2_c_out), .D(add1bit_3_d), .C_out(add1bit_3_c_out));
  ADD1BIT add1bit_4 (.A(add1bit_1_d), .B(add1bit_2_d), .C_in(add1bit_3_d), .D(add1bit_4_d), .C_out(add1bit_4_c_out));
  // ADD1BIT add1bit_5: pin names not known; wires that end beside it: add1bit_5_p1, add1bit_1_c_out, add1bit_4_c_out, add1bit_5_p4, add1bit_5_p5
  ADD1BIT add1bit_6 (.A(add1bit_4_d), .D(add1bit_5_p1), .C_out(add1bit_6_c_out));  // open: B, C_in
  ADD1BIT add1bit_7 (.A(add1bit_5_p4), .B(add1bit_3_c_out), .C_in(add1bit_6_c_out), .D(D[1]), .C_out(add1bit_7_c_out));
  ADD1BIT add1bit_8 (.A(add1bit_5_p5), .C_in(add1bit_7_c_out), .D(D[2]), .C_out(D[3]));  // open: B

  // Notes on the sheet:
  //   Attention, votre version de Logisim
  //   ne contient pas de tracker. Si vous
  //   enregistrez votre projet, toutes les
  //   informations du tracker seront
  //   définitivement effacées.
endmodule

module LOGIC_1BIT (
  input  [1:0] OPCODE_1_0,
  input  A,
  input  B,
  output F
);

  wire nand_1_out, nand_2_out, nand_3_out, nand_4_out, nand_5_out, nand_6_out, nand_7_out, nand_8_out;

  nand nand_1 (nand_1_out, A, A);
  nand nand_2 (nand_2_out, B, B);
  nand nand_3 (nand_3_out, A, B);
  nand nand_4 (nand_4_out, nand_1_out, nand_2_out);
  nand nand_5 (nand_5_out, A, nand_3_out);
  nand nand_6 (nand_6_out, nand_3_out, B);
  nand nand_7 (nand_7_out, nand_3_out, nand_3_out);
  nand nand_8 (nand_8_out, nand_5_out, nand_6_out);
  Multiplexer #(.select(2), .enable("false")) multiplexer_1 (
    .in0(nand_7_out), .in1(nand_4_out), .in2(nand_3_out), .in3(nand_8_out), .out(F), .sel(OPCODE_1_0));

  // Notes on the sheet:
  //   Attention, votre version de Logisim
  //   ne contient pas de tracker. Si vous
  //   enregistrez votre projet, toutes les
  //   informations du tracker seront
  //   définitivement effacées.
endmodule

module LOGIC_4BITS (
  input  [1:0] OPCODE_1_0,
  input  [3:0] A,
  input  [3:0] B,
  output [3:0] F
);

  LOGIC_1BIT logic_1bit_1 (.OPCODE_1_0(OPCODE_1_0), .A(A[0]), .B(B[0]), .F(F[0]));
  LOGIC_1BIT logic_1bit_2 (.OPCODE_1_0(OPCODE_1_0), .A(A[1]), .B(B[1]), .F(F[1]));
  LOGIC_1BIT logic_1bit_3 (.OPCODE_1_0(OPCODE_1_0), .A(A[2]), .B(B[2]), .F(F[2]));
  LOGIC_1BIT logic_1bit_4 (.OPCODE_1_0(OPCODE_1_0), .A(A[3]), .B(B[3]), .F(F[3]));

  // Notes on the sheet:
  //   Attention, votre version de Logisim
  //   ne contient pas de tracker. Si vous
  //   enregistrez votre projet, toutes les
  //   informations du tracker seront
  //   définitivement effacées.
endmodule
